// Logisim project FinalProj5.circ as structural Verilog: 14 circuits, main circuit Computer
module Computer (
);

  wire clock_1_out, clock_2_out, clock_3_out, cpu_1_buswriteenable, joystickcontoller_1_joystick_enable,
       keyboard_1_avail, keyboardcontroller_1_keyboardread, keyboardcontroller_1_writetobus,
       memorycontroller_1_writeenabletomem, memorycontroller_1_writetobus, rgb_video_1_p1, rgb_video_1_p2,
       rgb_video_1_p3, soundcontroller_1_we;
  wire [3:0] hexdisplay_1_datatoscreen, joystick_1_x, joystick_1_y;
  wire [6:0] keyboard_1_data, soundcontroller_1_volume, terminalcontroller_1_datatoterminal;
  wire [7:0] rgb_video_1_p4, rgb_video_1_p5;
  wire [13:0] soundcontroller_1_frequency;
  wire [23:0] memorycontroller_1_addresstomem, rgb_video_1_p6;
  wire [25:0] cpu_1_addresstobus;
  wire [31:0] controlled_buffer_1_out, cpu_1_datatobus, joystickcontoller_1_datatobus,
       keyboardcontroller_1_datatobus, memorycontroller_1_datatobus, memorycontroller_1_datatomem, ram_1_dout;

  RAM #(.addrWidth(24), .dataWidth(32), .enables("line")) ram_1 (
    .addr(memorycontroller_1_addresstomem), .we(memorycontroller_1_writeenabletomem), .clk(clock_1_out),
    .din(memorycontroller_1_datatomem), .dout(ram_1_dout));
  Clock clock_1 (.out(clock_1_out));
  // Probe on memorycontroller_1_datatomem
  // Probe on ram_1_dout
  // Probe on controlled_buffer_1_out
  Clock clock_2 (.out(clock_2_out));
  Keyboard keyboard_1 (
    .clk(clock_2_out), .re(keyboardcontroller_1_keyboardread), .avail(keyboard_1_avail),
    .data(keyboard_1_data));  // open: clr
  // Probe on keyboard_1_data
  Hex_Digit_Display hex_digit_display_1 (.value(hexdisplay_1_datatoscreen));  // open: dp
  // Probe on controlled_buffer_1_out
  // Probe on controlled_buffer_1_out
  MemoryController memorycontroller_1 (
    .DataFromMem(ram_1_dout), .WriteEnableFromBus(cpu_1_buswriteenable), .AddressFromBus(cpu_1_addresstobus),
    .DataFromBus(controlled_buffer_1_out), .AddressToMem(memorycontroller_1_addresstomem),
    .WriteEnableToMem(memorycontroller_1_writeenabletomem), .WriteToBus(memorycontroller_1_writetobus),
    .DataToMem(memorycontroller_1_datatomem), .DataToBus(memorycontroller_1_datatobus));
  CPU cpu_1 (
    .DataFromBus(controlled_buffer_1_out), .AddressToBus(cpu_1_addresstobus),
    .BusWriteEnable(cpu_1_buswriteenable), .DataToBus(cpu_1_datatobus));
  assign controlled_buffer_1_out = memorycontroller_1_writetobus ? memorycontroller_1_datatobus : 32'bz;  // Controlled_Buffer controlled_buffer_1
  // Probe on rgb_video_1_p3
  assign controlled_buffer_1_out = cpu_1_buswriteenable ? cpu_1_datatobus : 32'bz;  // Controlled_Buffer controlled_buffer_2
  // Probe on cpu_1_buswriteenable
  // Probe on controlled_buffer_1_out
  KeyboardController keyboardcontroller_1 (
    .KeyboardStatus(keyboard_1_avail), .DataFromBus(controlled_buffer_1_out), .KeyboardData(keyboard_1_data),
    .WriteEnableFromBus(cpu_1_buswriteenable), .AddressFromBus(cpu_1_addresstobus),
    .KeyboardRead(keyboardcontroller_1_keyboardread), .WriteToBus(keyboardcontroller_1_writetobus),
    .DataToBus(keyboardcontroller_1_datatobus));
  assign controlled_buffer_1_out = keyboardcontroller_1_writetobus ? keyboardcontroller_1_datatobus : 32'bz;  // Controlled_Buffer controlled_buffer_3
  HexDisplay hexdisplay_1 (
    .WriteEnableFromBus(cpu_1_buswriteenable), .DataFromBus(controlled_buffer_1_out),
    .AddressFromBus(cpu_1_addresstobus), .DataToScreen(hexdisplay_1_datatoscreen));
  Clock clock_3 (.out(clock_3_out));
  TTY tty_1 (.data(terminalcontroller_1_datatoterminal), .clk(clock_3_out), .we(rgb_video_1_p1));  // open: clr
  // RGB_Video #(.height(256), .scale(1), .width(256)) rgb_video_1: pin names not known; wires that end beside it: rgb_video_1_p1, rgb_video_1_p2, rgb_video_1_p3, rgb_video_1_p4, rgb_video_1_p5, rgb_video_1_p6
  Clock clock_4 (.out(rgb_video_1_p2));
  Joystick joystick_1 (.x(joystick_1_x), .y(joystick_1_y));
  // Probe on cpu_1_addresstobus
  // Probe on controlled_buffer_1_out
  TerminalController terminalcontroller_1 (
    .DataFromBus(controlled_buffer_1_out), .AddressFromBus(cpu_1_addresstobus),
    .WriteEnableFromBus(cpu_1_buswriteenable), .DataToTerminal(terminalcontroller_1_datatoterminal),
    .WriteToTerminal(rgb_video_1_p1));
  RGBController rgbcontroller_1 (
    .DataFromBus(controlled_buffer_1_out), .WriteEnable(cpu_1_buswriteenable),
    .AddressFromBus(cpu_1_addresstobus), .RGBX(rgb_video_1_p4), .RGBY(rgb_video_1_p5),
    .RGBColor(rgb_video_1_p6), .RGBWrite(rgb_video_1_p3));
  JoystickContoller joystickcontoller_1 (
    .X(joystick_1_x), .Y(joystick_1_y), .AddressFromBus(cpu_1_addresstobus),
    .DataToBus(joystickcontoller_1_datatobus), .JoyStick_enable(joystickcontoller_1_joystick_enable));
  SoundController soundcontroller_1 (
    .DataFromBus(controlled_buffer_1_out), .AddressFromBus(cpu_1_addresstobus),
    .WriteEnable(cpu_1_buswriteenable), .Frequency(soundcontroller_1_frequency), .WE(soundcontroller_1_we),
    .Volume(soundcontroller_1_volume));
  // Probe on terminalcontroller_1_datatoterminal
  // Probe on rgb_video_1_p1
  // Probe on rgb_video_1_p4
  // Probe on rgb_video_1_p6
  // Probe on rgb_video_1_p4
  // Probe on rgb_video_1_p3
  assign controlled_buffer_1_out = joystickcontoller_1_joystick_enable ? joystickcontoller_1_datatobus : 32'bz;  // Controlled_Buffer controlled_buffer_4
  // Probe on controlled_buffer_1_out
  // Buzzer buzzer_1: pin names not known; wires that end beside it: soundcontroller_1_frequency, soundcontroller_1_we, soundcontroller_1_volume, rgb_video_1_p3

  // Notes on the sheet:
  //   Write_enable
  //   Address
  //   Data
endmodule

module CPU (
  input  [31:0] DataFromBus,
  output [25:0] AddressToBus,
  output BusWriteEnable,
  output [31:0] DataToBus
);

  wire alu_1_equal, and_1_out, and_2_out, clock_1_out, control_1_beq, control_1_bne, control_1_immt_select,
       control_1_j, control_1_jal, control_1_jalr, control_1_jr, control_1_lw, control_1_reg_write_e,
       control_1_shift_select, not_1_out, or_1_out, or_2_out, or_3_out, or_4_out;
  wire [3:0] control_1_alu_code;
  wire [4:0] control_1_rd, control_1_rs, control_1_rt;
  wire [15:0] bit_extender_1_out;
  wire [31:0] adder_1_out, adder_2_out, alu_1_res, control_1_imm, control_1_shift_amount, multiplexer_1_out,
       multiplexer_2_out, multiplexer_3_out, multiplexer_4_out, multiplexer_5_out, multiplexer_6_out,
       multiplexer_7_out, regfile_1_rs_data, register_1_q, rom_1_data, shifter_1_out, shifter_2_out,
       shifter_3_out;

  // Probe on adder_1_out
  Adder #(.width(32)) adder_1 (.a(register_1_q), .b(32'h4), .out(adder_1_out));  // open: cin, cout
  Shifter #(.width(32)) shifter_1 (.in(control_1_imm), .\dist (5'b00010), .out(shifter_1_out));
  Adder #(.width(32)) adder_2 (.a(adder_1_out), .b(shifter_1_out), .out(adder_2_out));  // open: cin, cout
  // Probe on shifter_2_out
  Multiplexer #(.width(32)) multiplexer_1 (
    .in0(adder_1_out), .in1(adder_2_out), .out(multiplexer_1_out), .sel(or_4_out));
  // Probe on multiplexer_2_out
  Shifter #(.width(32)) shifter_2 (.in(control_1_imm), .\dist (5'b00010), .out(shifter_2_out));
  // Probe on regfile_1_rs_data
  // Probe on multiplexer_1_out
  Multiplexer #(.width(32)) multiplexer_2 (
    .in0(shifter_2_out), .in1(regfile_1_rs_data), .out(multiplexer_2_out), .sel(or_2_out));
  // Probe on control_1_imm
  Multiplexer #(.width(32)) multiplexer_3 (
    .in0(multiplexer_1_out), .in1(multiplexer_2_out), .out(multiplexer_3_out), .sel(or_3_out));
  // Probe on multiplexer_3_out
  Register #(.width(32)) register_1 (
    .D(multiplexer_3_out), .en(1'b1), .clk(clock_1_out), .Q(register_1_q));  // open: clr
  Clock clock_1 (.out(clock_1_out));
  Shifter #(.shift("lr"), .width(32)) shifter_3 (.in(register_1_q), .\dist (5'b00010), .out(shifter_3_out));
  Bit_Extender #(.in_width(32)) bit_extender_1 (.in(shifter_3_out), .out(bit_extender_1_out));
  // Probe on bit_extender_1_out
  ROM #(.addrWidth(16), .dataWidth(32)) rom_1 (.addr(bit_extender_1_out), .data(rom_1_data));
  // Probe on multiplexer_4_out
  Multiplexer #(.width(32)) multiplexer_4 (
    .in0(multiplexer_7_out), .in1(adder_1_out), .out(multiplexer_4_out), .sel(or_1_out));
  or or_1 (or_1_out, control_1_jalr, control_1_jal);
  // Probe on rom_1_data
  or or_2 (or_2_out, control_1_jalr, control_1_jr);
  or or_3 (or_3_out, control_1_jal, control_1_j, control_1_jalr, control_1_jr);
  regfile regfile_1 (
    .write(control_1_reg_write_e), .rd(control_1_rd), .rt(control_1_rt), .rs(control_1_rs),
    .rd_data(multiplexer_4_out), .rt_data(DataToBus), .rs_data(regfile_1_rs_data));
  // Probe on regfile_1_rs_data
  Control control_1 (
    .Inst(rom_1_data), .jr(control_1_jr), .jalr(control_1_jalr), .shift_select(control_1_shift_select),
    .ALU_code(control_1_alu_code), .shift_amount(control_1_shift_amount), .rd(control_1_rd),
    .rt(control_1_rt), .rs(control_1_rs), .imm(control_1_imm), .lw(control_1_lw), .sw(BusWriteEnable),
    .reg_write_e(control_1_reg_write_e), .beq(control_1_beq), .bne(control_1_bne),
    .immt_select(control_1_immt_select), .j(control_1_j), .jal(control_1_jal));
  or or_4 (or_4_out, and_1_out, and_2_out);
  // Probe on control_1_imm
  // Probe on control_1_rd
  // Probe on control_1_rt
  // Probe on control_1_rs
  and and_1 (and_1_out, control_1_bne, not_1_out);
  and and_2 (and_2_out, control_1_beq, alu_1_equal);
  Multiplexer #(.width(32)) multiplexer_5 (
    .in0(regfile_1_rs_data), .in1(control_1_shift_amount), .out(multiplexer_5_out),
    .sel(control_1_shift_select));
  Multiplexer #(.width(32)) multiplexer_6 (
    .in0(DataToBus), .in1(control_1_imm), .out(multiplexer_6_out), .sel(control_1_immt_select));
  not not_1 (not_1_out, alu_1_equal);
  // Probe on multiplexer_6_out
  // Probe on multiplexer_5_out
  // Probe on multiplexer_7_out
  // Probe on control_1_alu_code
  // Probe on alu_1_res
  ALU alu_1 (
    .ALU_CODE(control_1_alu_code), .OP1(multiplexer_5_out), .OP2(multiplexer_6_out), .Res(alu_1_res),
    .Equal(alu_1_equal));
  Multiplexer #(.width(32)) multiplexer_7 (
    .in0(alu_1_res), .in1(DataFromBus), .out(multiplexer_7_out), .sel(control_1_lw));
  Bit_Extender #(.in_width(32), .out_width(26)) bit_extender_2 (.in(alu_1_res), .out(AddressToBus));

  // Notes on the sheet:
  //   offset
  //   pc + 4
  //   offset
  //   rd_data
  //   any branch
  //   immediate
  //   j select
  //   Program Counter
  //   rs_data for jr and jalr
  //   contents of rom_1 (hex, n*v repeats v):
  //   10400019 201b0001 105b001b 201b0004 105b009b 201b0005 105b0037 201b0008 105b00a2 201b0009 105b0083
  //   201b000a 105b008a 201b000b 105b0089 201b000c 105b0089 201b003c 105b00ae 201b003d 105b00bd 201b003e
  //   105b00c3 201b003f 105b00c3 8000097 201df000 201b0000 b01af000 80000de 23bdfff4 23bb0000 afba0008
  //   209a0000 afaa0004 afab0000 200a000a 80502a 11400003 201a002d ac1aff00 42022 209a0000 200a000a
  //   34a001a d012 5810 23bdfffc afab0000 1740fffa 8fba0000 235a0030 ac1aff00 23bd0004 17bbfffb 8fab0000
  //   23bd0004 8faa0000 23bd0004 8fba0000 23bd0004 3400008 23bdfff4 afaa0000 afab0004 afba0008 200a000a
  //   201b0000 200b0030 8c1aff10 1340003f 8c1aff14 ac00ff10 134b0015 216b0001 134b0016 216b0001 134b0018
  //   216b0001 134b001a 216b0001 134b001c 216b0001 134b001e 216b0001 134b0020 216b0001 134b0022 216b0001
  //   134b0024 216b0001 134b0026 216b0001 1ad820 8000086 36a0018 d812 8000086 36a0018 d812 237b0001
  //   8000086 36a0018 d812 237b0002 8000086 36a0018 d812 237b0003 8000086 36a0018 d812 237b0004 8000086
  //   36a0018 d812 237b0005 8000086 36a0018 d812 237b0006 8000086 36a0018 d812 237b0007 8000086 36a0018
  //   d812 237b0008 8000086 36a0018 d812 237b0009 8000086 3601020 8faa0000 23bd0004 8fab0000 23bd0004
  //   8fba0000 23bd0004 3400008 23bdfffc afba0000 9019f000 3401020 344d020 b019f000 8fba0000 23bd0004
  //   3400008 8000097 ac04ff00 3400008 8c1bff10 13600003 8c1bff14 ac00ff10 23620000 3400008 23bdfffc
  //   afba0000 209a0000 8f5b0000 13600003 ac1bff00 235a0004 80000a3 8fba0000 23bd0004 3400008 23bdfff8
  //   afba0004 afa80000 20080001 209a0000 a8d82a 1760000a 11050009 8c1bff10 13600007 8c1bff14 13600005
  //   ac00ff10 af5b0000 235a0004 21080001 80000b2 af400000 8fba0004 8fa80000 23bd0008 3400008 23bdfff8
  //   afa40000 afa50004 8c04ffb0 8c05ffb4 201b0008 17640002 17650001 80000c1 8fa40000 8fa50004 23bd0008
  //   3400008 8fa40000 8fa50004 23bd0008 3400008 23bdfffc afa60000 ac04ffac ac05ffa4 8c08ffa8 8fa60000
  //   23bd0004 3400008 ac04ff41 3400008 ac04ff30 3400008 20100001 20150000 200d0000 2011000a 20020005 d00c
  //   20520000 251982a 12600006 2500018 9012 2110018 8012 2b2a820 80000e1 12a00008 2011000a 2b1001a a812
  //   5810 1b10018 6812 1ab6820 80000ed 1a0a820 2014005f 12d4000e 1254000d 2014002b 12d40018 12540017
  //   2014002d 12d40024 12540023 2014002a 12d40030 1254002f 2014002f 12d4003e 1254003d 80000de 200e002b
  //   12ce0013 124e0012 200e002d 12ce001f 124e001e 200e002a 12ce002c 124e002b 200e002f 12ce003a 124e0039
  //   80000de 22b70000 c000154 21a00000 177820 172020 20020001 d00c 80000de c000154 21a00000 1e02020
  //   20020001 d00c 1e07820 80000de 22b70000 c000154 21a00000 2e07822 2e02022 20020001 d00c 80000de
  //   c000154 21a00000 1e02022 20020001 d00c 1e07822 80000de 22b70000 c000154 21a00000 2e00018 7812 f2020
  //   20020001 d00c 80000de c000154 21a00000 1e00018 2012 20020001 d00c 47820 80000de 22b70000 c000154
  //   21a00000 2e0001a 7812 f2020 20020001 d00c 80000de c000154 21a00000 1e0001a 2012 20020001 d00c 47820
  //   80000de 20100001 20150000 200d0000 2011000a 20020005 d00c 20520000 251982a 12600006 2500018 9012
  //   2110018 8012 2b2a820 8000157 12a00008 2011000a 2b1001a a812 5810 1b10018 6812 1ab6820 8000163
  //   22560000 3e00008
  //   immediate for j and jal
  //   any jump
  //   offset
  //   imm
  //   rd
  //   rt
  //   rs
  //   immeidate
  //   beq and bne 
  //   shift amount
  //   rs_data
  //   shift_amount
  //   shift select
endmodule

module MemoryController (
  input  [25:0] AddressFromBus,
  input  WriteEnableFromBus,
  input  [31:0] DataFromBus,
  input  [31:0] DataFromMem,
  output [23:0] AddressToMem,
  output WriteEnableToMem,
  output WriteToBus,
  output [31:0] DataToMem,
  output [31:0] DataToBus
);

  wire comparator_1_lt;
  wire [25:0] shifter_1_out;

  Comparator #(.mode("unsigned"), .width(26)) comparator_1 (
    .a(AddressFromBus), .b(26'h3ffff00), .lt(comparator_1_lt));  // open: gt, eq
  and and_1 (WriteEnableToMem, comparator_1_lt, WriteEnableFromBus);
  and and_2 (WriteToBus, comparator_1_lt, ~WriteEnableFromBus);  // AND_Gate
  Shifter #(.shift("lr"), .width(26)) shifter_1 (.in(AddressFromBus), .\dist (5'b00010), .out(shifter_1_out));
  Bit_Extender #(.in_width(26), .out_width(24)) bit_extender_1 (.in(shifter_1_out), .out(AddressToMem));

  assign DataToBus = DataFromMem;
  assign DataToMem = DataFromBus;

  // Notes on the sheet:
  //   AddressFromBus: initial=0x3ffff00
endmodule

module KeyboardController (
  input  WriteEnableFromBus,
  input  [25:0] AddressFromBus,
  input  [31:0] DataFromBus,
  input  KeyboardStatus,
  input  [6:0] KeyboardData,
  output KeyboardRead,
  output WriteToBus,
  output [31:0] DataToBus
);

  wire and_1_out, and_2_out, comparator_1_eq, comparator_2_eq, not_1_out, or_1_out;
  wire [31:0] bit_extender_1_out, bit_extender_2_out, multiplexer_1_out;

  assign bit_extender_1_out = {{31{1'b0}}, KeyboardStatus};  // Bit_Extender bit_extender_1
  // Probe on KeyboardData
  assign bit_extender_2_out = {{25{1'b0}}, KeyboardData};  // Bit_Extender bit_extender_2
  not not_1 (not_1_out, WriteEnableFromBus);
  Comparator #(.mode("unsigned"), .width(26)) comparator_1 (
    .a(AddressFromBus), .b(26'h3ffff10), .eq(comparator_1_eq));  // open: gt, lt
  Comparator #(.mode("unsigned"), .width(26)) comparator_2 (
    .a(AddressFromBus), .b(26'h3ffff14), .eq(comparator_2_eq));  // open: gt, lt
  Multiplexer #(.width(32)) multiplexer_1 (
    .in0({32{1'b0}}), .in1(bit_extender_1_out), .out(multiplexer_1_out), .sel(and_2_out));
  and and_1 (and_1_out, comparator_2_eq, not_1_out);
  Multiplexer #(.width(32)) multiplexer_2 (
    .in0(multiplexer_1_out), .in1(bit_extender_2_out), .out(DataToBus), .sel(and_1_out));
  and and_2 (and_2_out, not_1_out, comparator_1_eq);
  // Probe on DataToBus
  and and_3 (KeyboardRead, WriteEnableFromBus, comparator_1_eq);
  or or_1 (or_1_out, comparator_1_eq, comparator_2_eq);
  and and_4 (WriteToBus, or_1_out, not_1_out);
endmodule

module RGBController (
  input  [31:0] DataFromBus,
  input  WriteEnable,
  input  [25:0] AddressFromBus,
  output [7:0] RGBX,
  output [7:0] RGBY,
  output [23:0] RGBColor,
  output RGBWrite
);

  wire and_1_out, and_2_out, and_3_out, clock_1_out, clock_2_out, clock_3_out, comparator_1_eq,
       comparator_2_eq, comparator_3_eq, comparator_4_eq;
  wire [31:0] register_1_q, register_2_q, register_3_q;

  // Probe on WriteEnable
  Comparator #(.mode("unsigned"), .width(26)) comparator_1 (
    .a(AddressFromBus), .b(26'h3ffff20), .eq(comparator_1_eq));  // open: gt, lt
  Comparator #(.mode("unsigned"), .width(26)) comparator_2 (
    .a(AddressFromBus), .b(26'h3ffff24), .eq(comparator_2_eq));  // open: gt, lt
  Comparator #(.mode("unsigned"), .width(26)) comparator_3 (
    .a(AddressFromBus), .b(26'h3ffff28), .eq(comparator_3_eq));  // open: gt, lt
  // Probe on DataFromBus
  Comparator #(.mode("unsigned"), .width(26)) comparator_4 (
    .a(AddressFromBus), .b(26'h3ffff2c), .eq(comparator_4_eq));  // open: gt, lt
  and and_1 (and_1_out, comparator_1_eq, WriteEnable);
  and and_2 (and_2_out, comparator_2_eq, WriteEnable);
  and and_3 (and_3_out, comparator_3_eq, WriteEnable);
  and and_4 (RGBWrite, comparator_4_eq, WriteEnable);
  Register #(.width(32)) register_1 (
    .D(DataFromBus), .en(and_1_out), .clk(clock_1_out), .Q(register_1_q));  // open: clr
  Clock clock_1 (.out(clock_1_out));
  Register #(.width(32)) register_2 (
    .D(DataFromBus), .en(and_2_out), .clk(clock_2_out), .Q(register_2_q));  // open: clr
  Clock clock_2 (.out(clock_2_out));
  Register #(.width(32)) register_3 (
    .D(DataFromBus), .en(and_3_out), .clk(clock_3_out), .Q(register_3_q));  // open: clr
  Clock clock_3 (.out(clock_3_out));
  Bit_Extender #(.in_width(32), .out_width(8), .\type ("zero")) bit_extender_1 (.in(register_1_q), .out(RGBX));
  Bit_Extender #(.in_width(32), .out_width(8), .\type ("zero")) bit_extender_2 (.in(register_2_q), .out(RGBY));
  Bit_Extender #(.in_width(32), .out_width(24), .\type ("zero")) bit_extender_3 (.in(register_3_q), .out(RGBColor));
endmodule

module TerminalController (
  input  [31:0] DataFromBus,
  input  [25:0] AddressFromBus,
  input  WriteEnableFromBus,
  output [6:0] DataToTerminal,
  output WriteToTerminal
);

  wire comparator_1_eq;

  Bit_Extender #(.in_width(32), .out_width(7)) bit_extender_1 (.in(DataFromBus), .out(DataToTerminal));
  Comparator #(.mode("unsigned"), .width(26)) comparator_1 (
    .a(AddressFromBus), .b(26'h3ffff00), .eq(comparator_1_eq));  // open: gt, lt
  and and_1 (WriteToTerminal, comparator_1_eq, WriteEnableFromBus);
endmodule

module regfile (
  input  write,
  input  [4:0] rd,
  input  [4:0] rt,
  input  [4:0] rs,
  input  [31:0] rd_data,
  output [31:0] rt_data,
  output [31:0] rs_data
);

  wire clock_1_out, clock_2_out, clock_3_out, clock_4_out, clock_5_out, clock_6_out, clock_7_out,
       clock_8_out, clock_9_out, clock_10_out, clock_11_out, clock_12_out, clock_13_out, clock_14_out,
       clock_15_out, clock_16_out, clock_17_out, clock_18_out, clock_19_out, clock_20_out, clock_21_out,
       clock_22_out, clock_23_out, clock_24_out, clock_25_out, clock_26_out, clock_27_out, clock_28_out,
       clock_29_out, clock_30_out, clock_31_out, clock_32_out, demultiplexer_1_out0, demultiplexer_1_out1,
       demultiplexer_1_out2, demultiplexer_1_out3, demultiplexer_1_out4, demultiplexer_1_out5,
       demultiplexer_1_out6, demultiplexer_1_out7, demultiplexer_1_out8, demultiplexer_1_out9,
       demultiplexer_1_out10, demultiplexer_1_out11, demultiplexer_1_out12, demultiplexer_1_out13,
       demultiplexer_1_out14, demultiplexer_1_out15, demultiplexer_1_out16, demultiplexer_1_out17,
       demultiplexer_1_out18, demultiplexer_1_out19, demultiplexer_1_out20, demultiplexer_1_out21,
       demultiplexer_1_out22, demultiplexer_1_out23, demultiplexer_1_out24, demultiplexer_1_out25,
       demultiplexer_1_out26, demultiplexer_1_out27, demultiplexer_1_out28, demultiplexer_1_out29,
       demultiplexer_1_out30, demultiplexer_1_out31;
  wire [31:0] a0_q, a1_q, a2_q, a3_q, at_q, gp_q, k0_q, k1_q, R0_q, ra_q, s0_q, s1_q, s2_q, s3_q, s4_q, s5_q,
       s6_q, s7_q, s8_q, sp_q, t0_q, t1_q, t2_q, t3_q, t4_q, t5_q, t6_q, t7_q, t8_q, t9_q, v0_q, v1_q;

  Multiplexer #(.select(5), .width(32)) multiplexer_1 (
    .in0(R0_q), .in1(at_q), .in2(v0_q), .in3(v1_q), .in4(a0_q), .in5(a1_q), .in6(a2_q), .in7(a3_q),
    .in8(t0_q), .in9(t1_q), .in10(t2_q), .in11(t3_q), .in12(t4_q), .in13(t5_q), .in14(t6_q), .in15(t7_q),
    .in16(s0_q), .in17(s1_q), .in18(s2_q), .in19(s3_q), .in20(s4_q), .in21(s5_q), .in22(s6_q), .in23(s7_q),
    .in24(t8_q), .in25(t9_q), .in26(k0_q), .in27(k1_q), .in28(gp_q), .in29(sp_q), .in30(s8_q), .in31(ra_q),
    .out(rs_data), .sel(rs));
  Multiplexer #(.select(5), .width(32)) multiplexer_2 (
    .in0(R0_q), .in1(at_q), .in2(v0_q), .in3(v1_q), .in4(a0_q), .in5(a1_q), .in6(a2_q), .in7(a3_q),
    .in8(t0_q), .in9(t1_q), .in10(t2_q), .in11(t3_q), .in12(t4_q), .in13(t5_q), .in14(t6_q), .in15(t7_q),
    .in16(s0_q), .in17(s1_q), .in18(s2_q), .in19(s3_q), .in20(s4_q), .in21(s5_q), .in22(s6_q), .in23(s7_q),
    .in24(t8_q), .in25(t9_q), .in26(k0_q), .in27(k1_q), .in28(gp_q), .in29(sp_q), .in30(s8_q), .in31(ra_q),
    .out(rt_data), .sel(rt));
  Clock clock_1 (.out(clock_1_out));
  Register #(.width(32)) R0 (.D({32{1'b0}}), .en(demultiplexer_1_out0), .clk(clock_2_out), .Q(R0_q));  // open: clr
  Clock clock_2 (.out(clock_2_out));
  Register #(.width(32)) s0 (.D(rd_data), .en(demultiplexer_1_out16), .clk(clock_1_out), .Q(s0_q));  // open: clr
  Register #(.width(32)) at (.D(rd_data), .en(demultiplexer_1_out1), .clk(clock_3_out), .Q(at_q));  // open: clr
  Clock clock_3 (.out(clock_3_out));
  Register #(.width(32)) s1 (.D(rd_data), .en(demultiplexer_1_out17), .clk(clock_4_out), .Q(s1_q));  // open: clr
  Clock clock_4 (.out(clock_4_out));
  Register #(.width(32)) v0 (.D(rd_data), .en(demultiplexer_1_out2), .clk(clock_5_out), .Q(v0_q));  // open: clr
  Clock clock_5 (.out(clock_5_out));
  Register #(.width(32)) s2 (.D(rd_data), .en(demultiplexer_1_out18), .clk(clock_6_out), .Q(s2_q));  // open: clr
  Clock clock_6 (.out(clock_6_out));
  Register #(.width(32)) s3 (.D(rd_data), .en(demultiplexer_1_out19), .clk(clock_7_out), .Q(s3_q));  // open: clr
  Clock clock_7 (.out(clock_7_out));
  Register #(.width(32)) v1 (.D(rd_data), .en(demultiplexer_1_out3), .clk(clock_8_out), .Q(v1_q));  // open: clr
  Clock clock_8 (.out(clock_8_out));
  Register #(.width(32)) a0 (.D(rd_data), .en(demultiplexer_1_out4), .clk(clock_9_out), .Q(a0_q));  // open: clr
  Clock clock_9 (.out(clock_9_out));
  Register #(.width(32)) s4 (.D(rd_data), .en(demultiplexer_1_out20), .clk(clock_10_out), .Q(s4_q));  // open: clr
  Clock clock_10 (.out(clock_10_out));
  Register #(.width(32)) a1 (.D(rd_data), .en(demultiplexer_1_out5), .clk(clock_11_out), .Q(a1_q));  // open: clr
  Clock clock_11 (.out(clock_11_out));
  Register #(.width(32)) s5 (.D(rd_data), .en(demultiplexer_1_out21), .clk(clock_12_out), .Q(s5_q));  // open: clr
  Clock clock_12 (.out(clock_12_out));
  Register #(.width(32)) a2 (.D(rd_data), .en(demultiplexer_1_out6), .clk(clock_13_out), .Q(a2_q));  // open: clr
  Clock clock_13 (.out(clock_13_out));
  Register #(.width(32)) s6 (.D(rd_data), .en(demultiplexer_1_out22), .clk(clock_14_out), .Q(s6_q));  // open: clr
  Clock clock_14 (.out(clock_14_out));
  Register #(.width(32)) a3 (.D(rd_data), .en(demultiplexer_1_out7), .clk(clock_15_out), .Q(a3_q));  // open: clr
  Clock clock_15 (.out(clock_15_out));
  Register #(.width(32)) s7 (.D(rd_data), .en(demultiplexer_1_out23), .clk(clock_16_out), .Q(s7_q));  // open: clr
  Clock clock_16 (.out(clock_16_out));
  Register #(.width(32)) t0 (.D(rd_data), .en(demultiplexer_1_out8), .clk(clock_17_out), .Q(t0_q));  // open: clr
  Clock clock_17 (.out(clock_17_out));
  Register #(.width(32)) t8 (.D(rd_data), .en(demultiplexer_1_out24), .clk(clock_18_out), .Q(t8_q));  // open: clr
  Clock clock_18 (.out(clock_18_out));
  Register #(.width(32)) t1 (.D(rd_data), .en(demultiplexer_1_out9), .clk(clock_19_out), .Q(t1_q));  // open: clr
  Clock clock_19 (.out(clock_19_out));
  Register #(.width(32)) t9 (.D(rd_data), .en(demultiplexer_1_out25), .clk(clock_20_out), .Q(t9_q));  // open: clr
  Clock clock_20 (.out(clock_20_out));
  Register #(.width(32)) t2 (.D(rd_data), .en(demultiplexer_1_out10), .clk(clock_21_out), .Q(t2_q));  // open: clr
  Clock clock_21 (.out(clock_21_out));
  Register #(.width(32)) k0 (.D(rd_data), .en(demultiplexer_1_out26), .clk(clock_22_out), .Q(k0_q));  // open: clr
  Clock clock_22 (.out(clock_22_out));
  Register #(.width(32)) k1 (.D(rd_data), .en(demultiplexer_1_out27), .clk(clock_23_out), .Q(k1_q));  // open: clr
  Clock clock_23 (.out(clock_23_out));
  Register #(.width(32)) t3 (.D(rd_data), .en(demultiplexer_1_out11), .clk(clock_24_out), .Q(t3_q));  // open: clr
  Clock clock_24 (.out(clock_24_out));
  Register #(.width(32)) t4 (.D(rd_data), .en(demultiplexer_1_out12), .clk(clock_25_out), .Q(t4_q));  // open: clr
  Clock clock_25 (.out(clock_25_out));
  Register #(.width(32)) gp (.D(rd_data), .en(demultiplexer_1_out28), .clk(clock_26_out), .Q(gp_q));  // open: clr
  Clock clock_26 (.out(clock_26_out));
  Register #(.width(32)) t5 (.D(rd_data), .en(demultiplexer_1_out13), .clk(clock_27_out), .Q(t5_q));  // open: clr
  Clock clock_27 (.out(clock_27_out));
  Register #(.width(32)) sp (.D(rd_data), .en(demultiplexer_1_out29), .clk(clock_28_out), .Q(sp_q));  // open: clr
  Clock clock_28 (.out(clock_28_out));
  Register #(.width(32)) t6 (.D(rd_data), .en(demultiplexer_1_out14), .clk(clock_29_out), .Q(t6_q));  // open: clr
  Clock clock_29 (.out(clock_29_out));
  Register #(.width(32)) s8 (.D(rd_data), .en(demultiplexer_1_out30), .clk(clock_30_out), .Q(s8_q));  // open: clr
  Clock clock_30 (.out(clock_30_out));
  Register #(.width(32)) ra (.D(rd_data), .en(demultiplexer_1_out31), .clk(clock_31_out), .Q(ra_q));  // open: clr
  Clock clock_31 (.out(clock_31_out));
  Register #(.width(32)) t7 (.D(rd_data), .en(demultiplexer_1_out15), .clk(clock_32_out), .Q(t7_q));  // open: clr
  Clock clock_32 (.out(clock_32_out));
  Demultiplexer #(.select(5)) demultiplexer_1 (
    .out0(demultiplexer_1_out0), .out1(demultiplexer_1_out1), .out2(demultiplexer_1_out2),
    .out3(demultiplexer_1_out3), .out4(demultiplexer_1_out4), .out5(demultiplexer_1_out5),
    .out6(demultiplexer_1_out6), .out7(demultiplexer_1_out7), .out8(demultiplexer_1_out8),
    .out9(demultiplexer_1_out9), .out10(demultiplexer_1_out10), .out11(demultiplexer_1_out11),
    .out12(demultiplexer_1_out12), .out13(demultiplexer_1_out13), .out14(demultiplexer_1_out14),
    .out15(demultiplexer_1_out15), .out16(demultiplexer_1_out16), .out17(demultiplexer_1_out17),
    .out18(demultiplexer_1_out18), .out19(demultiplexer_1_out19), .out20(demultiplexer_1_out20),
    .out21(demultiplexer_1_out21), .out22(demultiplexer_1_out22), .out23(demultiplexer_1_out23),
    .out24(demultiplexer_1_out24), .out25(demultiplexer_1_out25), .out26(demultiplexer_1_out26),
    .out27(demultiplexer_1_out27), .out28(demultiplexer_1_out28), .out29(demultiplexer_1_out29),
    .out30(demultiplexer_1_out30), .out31(demultiplexer_1_out31), .in(write), .sel(rd));
endmodule

module ALU (
  input  [3:0] ALU_CODE,
  input  [31:0] OP1,
  input  [31:0] OP2,
  output [31:0] Res,
  output Equal
);

  wire clock_1_out, clock_2_out, comparator_2_lt, comparator_3_eq, comparator_3_gt, or_1_out;
  wire [4:0] bit_extender_1_out, bit_extender_2_out;
  wire [31:0] adder_1_out, bit_extender_3_out, divider_1_out, divider_1_rem, HI_q, LO_q, multiplexer_1_out,
       multiplexer_2_out, multiplier_1_cout, multiplier_1_out, shifter_1_out, shifter_2_out, subtractor_1_out;

  Comparator #(.width(32)) comparator_1 (.a(OP1), .b(OP2), .eq(Equal));  // open: gt, lt
  Adder #(.width(32)) adder_1 (.a(OP1), .b(OP2), .out(adder_1_out));  // open: cin, cout
  Subtractor #(.width(32)) subtractor_1 (.a(OP1), .b(OP2), .out(subtractor_1_out));  // open: bin, bout
  Divider #(.width(32)) divider_1 (.a(OP1), .b(OP2), .out(divider_1_out), .rem(divider_1_rem));  // open: upper
  Multiplier #(.width(32)) multiplier_1 (
    .a(OP1), .b(OP2), .out(multiplier_1_out), .cout(multiplier_1_cout));  // open: cin
  Bit_Extender #(.in_width(32), .out_width(5)) bit_extender_1 (.in(OP1), .out(bit_extender_1_out));
  Bit_Extender #(.in_width(32), .out_width(5)) bit_extender_2 (.in(OP1), .out(bit_extender_2_out));
  Comparator #(.width(32)) comparator_2 (.a(OP1), .b(OP2), .lt(comparator_2_lt));  // open: gt, eq
  // Probe on 4'b1000
  Shifter #(.width(32)) shifter_1 (.in(OP2), .\dist (bit_extender_1_out), .out(shifter_1_out));
  Shifter #(.shift("lr"), .width(32)) shifter_2 (.in(OP2), .\dist (bit_extender_2_out), .out(shifter_2_out));
  // Probe on ALU_CODE
  Comparator #(.mode("unsigned"), .width(4)) comparator_3 (
    .a(ALU_CODE), .b(4'b1000), .gt(comparator_3_gt), .eq(comparator_3_eq));  // open: lt
  or or_1 (or_1_out, comparator_3_eq, comparator_3_gt);
  Register #(.width(32)) LO (.D(multiplexer_1_out), .en(or_1_out), .clk(clock_1_out), .Q(LO_q));  // open: clr
  Multiplexer #(.width(32)) multiplexer_1 (
    .in0(multiplier_1_out), .in1(divider_1_out), .out(multiplexer_1_out), .sel(comparator_3_gt));
  Clock clock_1 (.out(clock_1_out));
  Register #(.width(32)) HI (.D(multiplexer_2_out), .en(or_1_out), .clk(clock_2_out), .Q(HI_q));  // open: clr
  Multiplexer #(.width(32)) multiplexer_2 (
    .in0(multiplier_1_cout), .in1(divider_1_rem), .out(multiplexer_2_out), .sel(comparator_3_gt));
  Clock clock_2 (.out(clock_2_out));
  assign bit_extender_3_out = {{31{1'b0}}, comparator_2_lt};  // Bit_Extender bit_extender_3
  Multiplexer #(.select(4), .width(32)) multiplexer_3 (
    .in0(adder_1_out), .in1(subtractor_1_out), .in2(LO_q), .in3(HI_q), .in4(shifter_1_out),
    .in5(shifter_2_out), .in7(bit_extender_3_out), .out(Res), .sel(ALU_CODE));  // open: in6, in8, in9, in10, in11, in12, in13, in14, in15
endmodule

module Control (
  input  [31:0] Inst,
  output jr,
  output jalr,
  output shift_select,
  output [3:0] ALU_code,
  output [31:0] shift_amount,
  output [4:0] rd,
  output [4:0] rt,
  output [4:0] rs,
  output [31:0] imm,
  output lw,
  output sw,
  output reg_write_e,
  output beq,
  output bne,
  output immt_select,
  output j,
  output jal
);

  wire comparator_1_eq, comparator_2_eq, comparator_9_eq, comparator_11_eq, comparator_12_eq,
       comparator_13_eq, comparator_14_eq, comparator_15_eq, comparator_16_eq, comparator_17_eq,
       comparator_18_eq, comparator_19_eq, comparator_20_eq, or_1_out, or_3_out, or_4_out, or_5_out,
       or_6_out, or_8_out;
  wire [4:0] multiplexer_2_out, multiplexer_13_out;
  wire [5:0] multiplexer_1_out;
  wire [31:0] bit_extender_2_out;

  // Probe on multiplexer_1_out
  // Probe on Inst[5:0]
  // Probe on Inst[25:21]
  // Probe on Inst[15:11]
  Comparator #(.width(6)) comparator_1 (.a(Inst[31:26]), .b({6{1'b0}}), .eq(comparator_1_eq));  // open: gt, lt
  // Probe on Inst[31:26]
  Multiplexer #(.width(6)) multiplexer_1 (
    .in0(6'b001111), .in1(Inst[5:0]), .out(multiplexer_1_out), .sel(comparator_1_eq));
  Comparator #(.width(6)) comparator_2 (.a(Inst[31:26]), .b(6'b001000), .eq(comparator_2_eq));  // open: gt, lt
  Comparator #(.width(6)) comparator_3 (.a(Inst[31:26]), .b(6'b100011), .eq(lw));  // open: gt, lt
  Comparator #(.width(6)) comparator_4 (.a(Inst[31:26]), .b(6'b101011), .eq(sw));  // open: gt, lt
  Comparator #(.width(6)) comparator_5 (.a(Inst[31:26]), .b(6'b000100), .eq(beq));  // open: gt, lt
  Comparator #(.width(6)) comparator_6 (.a(Inst[31:26]), .b(6'b000101), .eq(bne));  // open: gt, lt
  Comparator #(.width(6)) comparator_7 (.a(Inst[31:26]), .b(6'b000010), .eq(j));  // open: gt, lt
  Comparator #(.width(6)) comparator_8 (.a(Inst[31:26]), .b(6'b000011), .eq(jal));  // open: gt, lt
  Comparator #(.width(6)) comparator_9 (.a(multiplexer_1_out), .b(6'b001100), .eq(comparator_9_eq));  // open: gt, lt
  Comparator #(.width(6)) comparator_10 (.a(multiplexer_1_out), .b(6'b001000), .eq(jr));  // open: gt, lt
  Comparator #(.width(6)) comparator_11 (.a(multiplexer_1_out), .b(6'b001001), .eq(comparator_11_eq));  // open: gt, lt
  Comparator #(.width(6)) comparator_12 (.a(multiplexer_1_out), .b(6'b101010), .eq(comparator_12_eq));  // open: gt, lt
  Comparator #(.width(6)) comparator_13 (.a(multiplexer_1_out), .b(6'b010010), .eq(comparator_13_eq));  // open: gt, lt
  Comparator #(.width(6)) comparator_14 (.a(multiplexer_1_out), .b(6'b010000), .eq(comparator_14_eq));  // open: gt, lt
  Comparator #(.width(6)) comparator_15 (.a(multiplexer_1_out), .b({6{1'b0}}), .eq(comparator_15_eq));  // open: gt, lt
  Comparator #(.width(6)) comparator_16 (.a(multiplexer_1_out), .b(6'b000010), .eq(comparator_16_eq));  // open: gt, lt
  Comparator #(.width(6)) comparator_17 (.a(multiplexer_1_out), .b(6'b011000), .eq(comparator_17_eq));  // open: gt, lt
  Comparator #(.width(6)) comparator_18 (.a(multiplexer_1_out), .b(6'b011010), .eq(comparator_18_eq));  // open: gt, lt
  Comparator #(.width(6)) comparator_19 (.a(multiplexer_1_out), .b(6'b100000), .eq(comparator_19_eq));  // open: gt, lt
  Comparator #(.width(6)) comparator_20 (.a(multiplexer_1_out), .b(6'b100010), .eq(comparator_20_eq));  // open: gt, lt
  or or_1 (or_1_out, comparator_2_eq, lw);
  or or_2 (shift_select, comparator_15_eq, comparator_16_eq);
  or or_3 (or_3_out, comparator_17_eq, comparator_18_eq);
  Multiplexer #(.width(5)) multiplexer_2 (
    .in0(Inst[15:11]), .in1(Inst[20:16]), .out(multiplexer_2_out), .sel(or_1_out));
  or or_4 (or_4_out, sw, beq, bne, j);
  or or_5 (or_5_out, j, jal);
  or or_6 (or_6_out, comparator_13_eq, comparator_14_eq);
  or or_7 (jalr, comparator_9_eq, comparator_11_eq);
  Multiplexer #(.width(4)) multiplexer_3 (.in1(4'b0111), .out(ALU_code), .sel(comparator_12_eq));  // open: in0
  Multiplexer #(.width(4)) multiplexer_4 (.in1(4'b0010), .out(ALU_code), .sel(comparator_13_eq));  // open: in0
  Multiplexer #(.width(4)) multiplexer_5 (.in1(4'b0011), .out(ALU_code), .sel(comparator_14_eq));  // open: in0
  Multiplexer #(.width(4)) multiplexer_6 (.in1(4'b0100), .out(ALU_code), .sel(comparator_15_eq));  // open: in0
  Multiplexer #(.width(4)) multiplexer_7 (.in1(4'b0101), .out(ALU_code), .sel(comparator_16_eq));  // open: in0
  Multiplexer #(.width(4)) multiplexer_8 (.in1(4'b1000), .out(ALU_code), .sel(comparator_17_eq));  // open: in0
  Multiplexer #(.width(4)) multiplexer_9 (.in1(4'b1001), .out(ALU_code), .sel(comparator_18_eq));  // open: in0
  Multiplexer #(.width(4)) multiplexer_10 (.in1(4'b0000), .out(ALU_code), .sel(comparator_19_eq));  // open: in0
  Multiplexer #(.width(4)) multiplexer_11 (.in1(4'b0001), .out(ALU_code), .sel(comparator_20_eq));  // open: in0
  Multiplexer #(.width(4)) multiplexer_12 (.in1(4'b0000), .out(ALU_code), .sel(comparator_2_eq));  // open: in0
  or or_8 (or_8_out, or_3_out, or_4_out);
  or or_9 (immt_select, jalr, lw, sw, comparator_2_eq, jal);
  assign shift_amount = {{27{Inst[10]}}, Inst[10:6]};  // Bit_Extender bit_extender_1
  Multiplexer #(.width(5)) multiplexer_13 (
    .in0(multiplexer_2_out), .in1({5{1'b1}}), .out(multiplexer_13_out), .sel(jal));
  not not_1 (reg_write_e, or_8_out);
  assign bit_extender_2_out = {{16{Inst[15]}}, Inst[15:0]};  // Bit_Extender bit_extender_2
  Multiplexer #(.width(5)) multiplexer_14 (.in0(multiplexer_13_out), .in1(5'b11010), .out(rd), .sel(comparator_9_eq));
  Multiplexer #(.width(32)) multiplexer_15 (
    .in0(bit_extender_2_out), .in1({{6{1'b0}}, Inst[25:0]}), .out(imm), .sel(or_5_out));

  assign rs = Inst[25:21];
  assign rt = Inst[20:16];

  // Notes on the sheet:
  //   imm
  //   funccode
  //   sa
  //   rd
  //   rt
  //   rs
  //   opcode
  //   addi
  //   lw
  //   sw
  //   beq
  //   bne
  //   j
  //   jal
  //   syscall
  //   jr
  //   jalr
  //   slt
  //   mflw
  //   mfhi
  //   sll
  //   srl
  //   mult
  //   div
  //   add
  //   sub
  //   target
  //   immediate
endmodule

module JoystickContoller (
  input  [3:0] X,
  input  [3:0] Y,
  input  [25:0] AddressFromBus,
  output [31:0] DataToBus,
  output JoyStick_enable
);

  wire comparator_1_eq, comparator_2_eq;
  wire [3:0] multiplexer_1_out;

  Comparator #(.mode("unsigned"), .width(26)) comparator_1 (
    .a(AddressFromBus), .b(26'h3ffffac), .eq(comparator_1_eq));  // open: gt, lt
  Comparator #(.mode("unsigned"), .width(26)) comparator_2 (
    .a(AddressFromBus), .b(26'h3ffffb0), .eq(comparator_2_eq));  // open: gt, lt
  Multiplexer #(.width(4)) multiplexer_1 (.in0(X), .in1(Y), .out(multiplexer_1_out), .sel(comparator_2_eq));
  assign DataToBus = {{28{1'b0}}, multiplexer_1_out};  // Bit_Extender bit_extender_1
  or or_1 (JoyStick_enable, comparator_1_eq, comparator_2_eq);
endmodule

module SoundController (
  input  [31:0] DataFromBus,
  input  [25:0] AddressFromBus,
  input  WriteEnable,
  output [13:0] Frequency,
  output WE,
  output [6:0] Volume
);

  wire and_1_out, and_3_out, comparator_1_eq, comparator_2_eq, comparator_3_eq;
  wire [31:0] register_1_q, register_2_q;

  Comparator #(.mode("unsigned"), .width(26)) comparator_1 (
    .a(AddressFromBus), .b(26'h3ffffa4), .eq(comparator_1_eq));  // open: gt, lt
  Comparator #(.mode("unsigned"), .width(26)) comparator_2 (
    .a(AddressFromBus), .b(26'h3ffffa8), .eq(comparator_2_eq));  // open: gt, lt
  Comparator #(.mode("unsigned"), .width(26)) comparator_3 (
    .a(AddressFromBus), .b(26'h3ffffac), .eq(comparator_3_eq));  // open: gt, lt
  and and_1 (and_1_out, comparator_1_eq, WriteEnable);
  and and_2 (WE, comparator_2_eq, WriteEnable);
  and and_3 (and_3_out, comparator_3_eq, WriteEnable);
  Register #(.width(32)) register_1 (.D(DataFromBus), .en(and_1_out), .Q(register_1_q));  // open: clk, clr
  Register #(.width(32)) register_2 (.D(DataFromBus), .en(and_3_out), .Q(register_2_q));  // open: clk, clr
  Bit_Extender #(.in_width(32), .out_width(14), .\type ("zero")) bit_extender_1 (.in(register_1_q), .out(Frequency));
  Bit_Extender #(.in_width(32), .out_width(7), .\type ("zero")) bit_extender_2 (.in(register_2_q), .out(Volume));
endmodule

module RGBLEDCont (
  input  [31:0] DataFromBus,
  input  [25:0] AddressFromBus,
  input  WriteEnable,
  output [7:0] RGBX,
  output [7:0] RGBY,
  output [23:0] RGBColor,
  output RGBWrite
);

  wire clock_1_out, comparator_4_eq, demultiplexer_1_out9, demultiplexer_1_out10, demultiplexer_1_out12;
  wire [2:0] comparator_1_eq;
  wire [7:0] bit_extender_1_out;
  wire [23:0] bit_extender_2_out;

  Comparator #(.width(26)) comparator_1 (.a(AddressFromBus), .b(26'h3ffff20), .eq(comparator_1_eq[0]));  // open: gt, lt
  Comparator #(.width(26)) comparator_2 (.a(AddressFromBus), .b(26'h3ffff24), .eq(comparator_1_eq[1]));  // open: gt, lt
  Comparator #(.width(26)) comparator_3 (.a(AddressFromBus), .b(26'h3ffff28), .eq(comparator_1_eq[2]));  // open: gt, lt
  Comparator #(.width(26)) comparator_4 (.a(AddressFromBus), .b(26'h3ffff2c), .eq(comparator_4_eq));  // open: gt, lt
  Demultiplexer #(.select(4)) demultiplexer_1 (
    .out9(demultiplexer_1_out9), .out10(demultiplexer_1_out10), .out12(demultiplexer_1_out12), .in(1'b1),
    .sel({WriteEnable, comparator_1_eq}));  // open: out0, out1, out2, out3, out4, out5, out6, out7, out8, out11, out13, out14, out15
  // Probe on {WriteEnable, comparator_1_eq}
  Bit_Extender #(.in_width(32), .out_width(8), .\type ("zero")) bit_extender_1 (
    .in(DataFromBus), .out(bit_extender_1_out));
  Bit_Extender #(.in_width(32), .out_width(24), .\type ("zero")) bit_extender_2 (
    .in(DataFromBus), .out(bit_extender_2_out));
  Clock clock_1 (.out(clock_1_out));
  Register register_1 (.D(bit_extender_1_out), .en(demultiplexer_1_out9), .clk(clock_1_out), .Q(RGBX));  // open: clr
  Register register_2 (.D(bit_extender_1_out), .en(demultiplexer_1_out10), .clk(clock_1_out), .Q(RGBY));  // open: clr
  Register #(.width(24)) register_3 (
    .D(bit_extender_2_out), .en(demultiplexer_1_out12), .clk(clock_1_out), .Q(RGBColor));  // open: clr
  and and_1 (RGBWrite, WriteEnable, comparator_4_eq);

  // Notes on the sheet:
  //   10001
  //   10010
  //   10100
  //   11000
endmodule

module SpeakController (
  input  [31:0] DataFromBus,
  input  [25:0] AddressFromBus,
  input  WriteEnabled,
  output PlayMusic,
  output [1:0] ToneSelect,
  output [13:0] Hz,
  output [6:0] Volume
);

  wire clock_1_out, demultiplexer_1_out3, demultiplexer_1_out5, demultiplexer_1_out9, demultiplexer_1_out17;
  wire [4:1] comparator_4_eq;
  wire [31:0] MHz_q, OnOff_q, Tone_q, Vol_q;

  Demultiplexer #(.select(5)) demultiplexer_1 (
    .out3(demultiplexer_1_out3), .out5(demultiplexer_1_out5), .out9(demultiplexer_1_out9),
    .out17(demultiplexer_1_out17), .in(1'b1), .sel({comparator_4_eq, WriteEnabled}));  // open: out0, out1, out2, out4, out6, out7, out8, out10, out11, out12, out13, out14, out15, out16, out18, out19, out20, out21, out22, out23, out24, out25, out26, out27, out28, out29, out30, out31
  Clock clock_1 (.out(clock_1_out));
  Register #(.width(32)) OnOff (
    .D(DataFromBus), .en(demultiplexer_1_out3), .clk(clock_1_out), .Q(OnOff_q));  // open: clr
  Register #(.width(32)) Tone (
    .D(DataFromBus), .en(demultiplexer_1_out17), .clk(clock_1_out), .Q(Tone_q));  // open: clr
  Register #(.width(32)) MHz (.D(DataFromBus), .en(demultiplexer_1_out9), .clk(clock_1_out), .Q(MHz_q));  // open: clr
  Register #(.width(32)) Vol (.D(DataFromBus), .en(demultiplexer_1_out5), .clk(clock_1_out), .Q(Vol_q));  // open: clr
  // Probe on {comparator_4_eq, WriteEnabled}
  // Probe on 26'h3ffff40
  // Probe on 26'h3ffff48
  // Probe on 26'h3ffff4c
  Comparator #(.width(26)) comparator_1 (.a(AddressFromBus), .b(26'h3ffff40), .eq(comparator_4_eq[4]));  // open: gt, lt
  Comparator #(.width(26)) comparator_2 (.a(AddressFromBus), .b(26'h3ffff44), .eq(comparator_4_eq[3]));  // open: gt, lt
  Comparator #(.width(26)) comparator_3 (.a(AddressFromBus), .b(26'h3ffff48), .eq(comparator_4_eq[2]));  // open: gt, lt
  Comparator #(.width(26)) comparator_4 (.a(AddressFromBus), .b(26'h3ffff4c), .eq(comparator_4_eq[1]));  // open: gt, lt
  Bit_Extender #(.in_width(32), .out_width(1)) bit_extender_1 (.in(OnOff_q), .out(PlayMusic));
  Bit_Extender #(.in_width(32), .out_width(2)) bit_extender_2 (.in(Tone_q), .out(ToneSelect));
  Bit_Extender #(.in_width(32), .out_width(14)) bit_extender_3 (.in(MHz_q), .out(Hz));
  Bit_Extender #(.in_width(32), .out_width(7)) bit_extender_4 (.in(Vol_q), .out(Volume));
endmodule

module HexDisplay (
  input  WriteEnableFromBus,
  input  [31:0] DataFromBus,
  input  [25:0] AddressFromBus,
  output [3:0] DataToScreen
);

  wire and_1_out, comparator_1_eq;
  wire [3:0] bit_extender_1_out;

  Comparator #(.mode("unsigned"), .width(26)) comparator_1 (
    .a(AddressFromBus), .b(26'h3fff000), .eq(comparator_1_eq));  // open: gt, lt
  Bit_Extender #(.in_width(32), .out_width(4), .\type ("zero")) bit_extender_1 (
    .in(DataFromBus), .out(bit_extender_1_out));
  Multiplexer #(.width(4)) multiplexer_1 (.in0(4'b0000), .in1(bit_extender_1_out), .out(DataToScreen), .sel(and_1_out));
  and and_1 (and_1_out, WriteEnableFromBus, comparator_1_eq);
endmodule
